# Fritzing sketch final_diag (saved by Fritzing 0.9.3b)
breadboards: 1

parts:
  Part1 = Arduino Uno (Rev3)
  Part2 = RFM69W
  SEN1 = Pulse Sensor [package=SIP-3]
  Stretch_sensor = Textile Stretch Sensor [part_number=PW052]
  R1 = Resistor [tolerance=±5% resistance=1k package="2010 [SMD]"]
  Heating_Pad = Heating Pad
  MOSFET = Basic FET P-Channel [package="DPak [SMD]"]
  BAT1 = BC9VPC [package=bc9vpc]
  U1 = 74HC595 [package="DIP16 [THT]"]
  R3 = Resistor [tolerance=±5% resistance=1k package="2010 [SMD]"]
  R4 = Resistor [tolerance=±5% resistance=1k package="2010 [SMD]"]
  R5 = Resistor [tolerance=±5% resistance=1k package="2010 [SMD]"]
  R6 = Resistor [tolerance=±5% resistance=1k package="2010 [SMD]"]
  R7 = Resistor [tolerance=±5% resistance=1k package="2010 [SMD]"]
  R8 = Resistor [tolerance=±5% resistance=1k package="2010 [SMD]"]
  R9 = Resistor [tolerance=±5% resistance=1k package="2010 [SMD]"]
  R10 = Resistor [tolerance=±5% resistance=1k package="2010 [SMD]"]
  LED1 = smd LED [color="Red (633nm)" package="1206 [SMD]"]
  LED2 = smd LED [color="Red (633nm)" package="1206 [SMD]"]
  LED3 = smd LED [color="Red (633nm)" package="1206 [SMD]"]
  LED4 = smd LED [color="Red (633nm)" package="1206 [SMD]"]
  LED5 = smd LED [color="Red (633nm)" package="1206 [SMD]"]
  LED6 = smd LED [color="Red (633nm)" package="1206 [SMD]"]
  LED7 = smd LED [color="Red (633nm)" package="1206 [SMD]"]
  LED8 = smd LED [color="Red (633nm)" package="1206 [SMD]"]

nets:
  N1: Part1.A0, SEN1.Signal
  GND: Part1.A1, Part1.GND, Part2.GND, SEN1.GND, R1.Pin_1, MOSFET.source, BAT1.V-, U1.GND, U1.OE, LED1.cathode, LED2.cathode, LED3.cathode, LED4.cathode, LED5.cathode, LED6.cathode, LED7.cathode, LED8.cathode
  N2: Part1.D9_PWM, MOSFET.Gate
  N3: Part1.D10_PWM/SS, Part2.NSS
  N4: Part1.D11_PWM/MOSI, Part2.MOSI
  N5: Part1.D12/MISO, Part2.MISO
  N6: Part1.D13/SCK, Part2.SCK
  N7: Part1.D2, Part2.DIO0
  N8: Part1.D4, U1.DS
  N9: Part1.D5_PWM, U1.ST_CP
  N10: Part1.D6_PWM, U1.SH_CP
  3V3: Part1.3V3, Part2.3V3
  VCC: Part1.5V, SEN1.VCC, Stretch_sensor.pin_1, U1.MR, U1.VCC
  N11: Stretch_sensor.pin_0, R1.Pin_0
  N12: Heating_Pad.pin_0, MOSFET.drain
  N13: Heating_Pad.pin_1, BAT1.V+
  N14: U1.Q1, R4.Pin_1
  N15: U1.Q2, R3.Pin_1
  N16: U1.Q3, R5.Pin_1
  N17: U1.Q4, R9.Pin_1
  N18: U1.Q5, R10.Pin_1
  N19: U1.Q6, R6.Pin_1
  N20: U1.Q7, R7.Pin_1
  N21: U1.Q0, R8.Pin_1
  N22: R3.Pin_0, LED4.anode
  N23: R4.Pin_0, LED2.anode
  N24: R5.Pin_0, LED3.anode
  N25: R6.Pin_0, LED6.anode
  N26: R7.Pin_0, LED5.anode
  N27: R8.Pin_0, LED1.anode
  N28: R9.Pin_0, LED8.anode
  N29: R10.Pin_0, LED7.anode

notes:
  Heart shape of LED's that will flash if heartrates are synchronized
  Heating pad output for breathing
  Stretch sensor to sense breathing
  Pulse sensor for heartrate
  RFM69 for radio transmition

custom parts:
  Pulse Sensor: Pulse Sensor Optical Heart Beat Sensor
  Heating Pad: A thermoresistant material with an embeded conductor that dissipates electrical energy into heat.
